# Fritzing sketch weatherlox-esp-pcb (saved by Fritzing 1.0.6)
circuit board: 9cm x 4cm

parts:
  R1 = Resistor [tolerance=±5% resistance=10k power=0.25W package=THT]
  R6 = Resistor [tolerance=±5% resistance=2.2k power=0.25W package=THT]
  R4 = Resistor [tolerance=±5% resistance=2.2k power=0.25W package=THT]
  R3 = Resistor [tolerance=±5% resistance=1.5k power=0.25W package=THT]
  R5 = Resistor [tolerance=±5% resistance=1.5k power=0.25W package=THT]
  ADS1115 = Adafruit ADS1115 16Bit I2C ADC [part_number="Adafruit #1085"]
  ESP32-DevKitC_v4 = ESP32 DevKitc V4
  MP1584EN = SBX DSUN [package=THT]
  R2 = Resistor [tolerance=±5% resistance=10k power=0.25W package=THT]
  Light3 = screw terminal, 3 pins
  Temp1 = screw terminal, 2 pins
  Temp2 = screw terminal, 2 pins
  Light2 = screw terminal, 2 pins
  Wind1 = screw terminal, 2 pins
  Wind2 = screw terminal, 2 pins
  RainA = screw terminal, 2 pins
  RainT = screw terminal, 3 pins
  GND = screw terminal, 2 pins
  +12V = screw terminal, 2 pins
  Light1 = screw terminal, 2 pins

nets:
  N1: R1.Pin_0, ESP32-DevKitC_v4.Pin_11, RainA.pin2
  GND: R1.Pin_1, R6.Pin_0, R4.Pin_0, ADS1115.GND, ESP32-DevKitC_v4.Pin_14, ESP32-DevKitC_v4.Pin_32, ESP32-DevKitC_v4.Pin_38, MP1584EN.GND, Temp1.pin2, Wind1.pin2, RainT.pin2, GND.pin1, GND.pin2, Light1.pin2
  N2: R6.Pin_1, R5.Pin_1, ADS1115.AIN2
  N3: R4.Pin_1, R3.Pin_1, ADS1115.AIN3
  N4: R3.Pin_0, Wind2.pin2
  N5: R5.Pin_0, Wind2.pin1
  N6: ADS1115.AIN1, Light3.pin2
  N7: ADS1115.AIN0, Light3.pin1
  N8: ADS1115.SDA, ESP32-DevKitC_v4.Pin_33, Temp2.pin1, Light2.pin1
  N9: ADS1115.SCL, ESP32-DevKitC_v4.Pin_36, Temp2.pin2, Light2.pin2
  N10: ADS1115.VDD, ESP32-DevKitC_v4.Pin_1, R2.Pin_1, Temp1.pin1, RainA.pin1, Light1.pin1
  N11: ESP32-DevKitC_v4.Pin_8, Light3.pin3
  N12: ESP32-DevKitC_v4.Pin_9, R2.Pin_0, RainT.pin3
  N13: ESP32-DevKitC_v4.Pin_19, MP1584EN.+VOUT
  N14: MP1584EN.+VIN, Wind1.pin1, RainT.pin1, +12V.pin1, +12V.pin2

notes:
  Version 1.00
  (c) Michael Schlenstedt
  WeatherLox

custom parts:
  Adafruit ADS1115 16Bit I2C ADC: For microcontrollers without an analog-to-digital converter or when you want a higher-precision ADC, the ADS1115 provides 16-bit precision at 860 samples/second over I2C. The chip can be configured as 4 single-ended input channels, or two differential channels. As a nice bonus, it even includes a programmable gain amplifier, up to x16, to help boost up smaller single/differential signals to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
  ESP32 DevKitc V4: ESP32-DevKitC board with ESP32-WROOM-32 module. ESP32-DevKitC V4 is a small-sized ESP32-based development board produced by Espressif. Most of the pins on the ESP module are broken out to the pin headers on the board. The pins D0, D1, D2, D3, CMD and CLK are used internally for communication between ESP32 and SPI flash memory. They are grouped on both sides near the USB connector. Avoid using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
  SBX DSUN: SBX DSUN input voltage 4.5 - 28V DC output voltage .8v to 20VDC (step down converter) Output current 3A max
