# Fritzing sketch weatherlox-solar-pcb (saved by Fritzing 1.0.6)
circuit board: 9cm x 4cm

parts:
  VEML7700 = VEML7700 [part_number="Adafruit #4162"]
  GUVA-S12SD = GUVA-S12SD
  KY-018 = KY-018 Photoresistor Module [package="Breakout board"]
  C1 = Electrolytic Capacitor [capacitance=220µF voltage=25V package="100 mil [THT, electrolytic]"]
  Light3 = screw terminal, 3 pins
  S+S- = screw terminal, 2 pins
  INS219 = INA219 High Side DC Current Sensor Breakout [part_number=904]
  Light1 = screw terminal, 2 pins
  Light2 = screw terminal, 2 pins
  GY-AS3935 = female pin header, 11 pins [form="♀ (female)"]

nets:
  3.3V: VEML7700.3.3V, GUVA-S12SD.Pin_3, KY-018.Vin, C1.+, INS219.VCC, Light1.pin1, GY-AS3935.pin1, GY-AS3935.pin7, GY-AS3935.pin9, GY-AS3935.pin10, GY-AS3935.pin11
  GND: VEML7700.GND, GUVA-S12SD.Pin_2, KY-018.-, C1.-, INS219.GND, Light1.pin2, GY-AS3935.pin2, GY-AS3935.pin5, GY-AS3935.pin6
  N1: VEML7700.SCL, INS219.SCL, Light2.pin2, GY-AS3935.pin3
  N2: VEML7700.SDA, INS219.SDA, Light2.pin1, GY-AS3935.pin4
  N3: GUVA-S12SD.Pin_1, Light3.pin2
  N4: KY-018.S, Light3.pin1
  N5: Light3.pin3, GY-AS3935.pin8
  N6: S+S-.pin1, INS219.VIN+
  N7: S+S-.pin2, INS219.VIN-

notes:
  Version 1.00
  (c) Michael Schlenstedt
  WeatherLox

custom parts:
  GUVA-S12SD: GUVA-S12SD S12SD UV Detection Light Intensity Sensor Ultraviolet.
  KY-018 Photoresistor Module: KY-018 Photoresistor module, used to measure light intensity. It can determine the presence or absence of light.
  INA219 High Side DC Current Sensor Breakout: This breakout board will solve all your power-monitoring problems. Instead of struggling with two multimeters, you can just use the handy INA219B chip on this breakout to both measure both the high side voltage and DC current draw over I2C with 1% precision. Most current-measuring devices such as our current panel meter are only good for low side measuring. That means that unless you want to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
